# Fritzing sketch HapticDrivers (saved by Fritzing 1.0.0d)
perfboards: 2

parts:
  J1 = female pin header, 5 pins [form="♀ (female)"]
  J2 = female pin header, 5 pins [form="♀ (female)"]  # not connected
  J3 = female pin header, 5 pins [form="♀ (female)"]
  J4 = female pin header, 5 pins [form="♀ (female)"]
  J5 = female pin header, 3 pins [form="♀ (female)"]
  J6 = female pin header, 3 pins [form="♀ (female)"]
  J7 = female pin header, 4 pins [form="♀ (female)"]
  J8 = Screw terminal - 2 pins [package=THT]
  J9 = Screw terminal - 2 pins [package=THT]
  IC1 = IC, DIP package, 16 pins [chip_label=IC]
  J10 = female pin header, 2 pins [form="♀ (female)"]
  IC2 = IC, DIP package, 8 pins [chip_label=IC]
  J11 = female pin header, 4 pins [form="♀ (female)"]
  R1 = Resistor [tolerance=±5% power=0.25W resistance=32.5k package=THT]  # not connected
  R2 = Temperature Sensor (Thermistor) [thermistor_type=NTC package=THT]
  J12 = female pin header, 2 pins [form="♀ (female)"]
  J13 = female pin header, 2 pins [form="♀ (female)"]
  R3 = Resistor [tolerance=±5% power=0.25W resistance=50k package=THT]
  R4 = Basic Flex Resistor
  R5 = Resistor [tolerance=±5% power=0.25W resistance=100 package=THT]
  R6 = Resistor [tolerance=±5% power=0.25W resistance=100 package=THT]
  C1 = Ceramic Capacitor [capacitance=10nF voltage=35V package="100 mil [THT, multilayer]"]
  C2 = Ceramic Capacitor [capacitance=10nF voltage=35V package="100 mil [THT, multilayer]"]
  J14 = Piezo Speaker
  J15 = Peltier Element
  J16 = Piezo Speaker

nets:
  N1: J1.pin1, J5.pin1
  N2: J1.pin2, J5.pin2
  N3: J1.pin3, J5.pin3
  N4: J1.pin5, J3.pin5
  N5: J3.pin1, J6.pin1
  N6: J3.pin2, J6.pin2
  N7: J3.pin3, J6.pin3
  N8: J3.pin4, J7.pin2, IC1.pin4
  N9: J4.pin2, J9.pin1, J16.pin2
  N10: J4.pin5, J9.pin2, J16.pin1
  N11: J7.pin3, IC1.pin2
  N12: J7.pin4, IC1.pin7
  N13: J8.pin1, J14.pin2
  N14: J8.pin2, J14.pin1
  N15: IC1.pin3, J10.pin1, J15.pin2
  N16: IC1.pin5, IC1.pin12
  N17: IC1.pin6, J10.pin2, J15.pin1
  N18: IC2.pin1, IC2.pin2, R6.Pin_1
  N19: IC2.pin3, R2.pin_0, J13.pin2
  N20: IC2.pin4, J11.pin3
  N21: IC2.pin5, J12.pin1, R4.Pin_2
  N22: IC2.pin7, R5.Pin_1
  N23: IC2.pin8, R3.Pin_0
  N24: J11.pin1, C2.1
  N25: J11.pin4, C1.0
  N26: R2.pin_1, J13.pin1
  N27: J12.pin2, R4.pin_1
  N28: R5.Pin_0, C2.0
  N29: R6.Pin_0, C1.1
