# Fritzing sketch Microcontroller (saved by Fritzing 1.0.0d)
perfboards: 1

parts:
  J1 = female pin header, 22 pins [form="♀ (female)"]
  J2 = female pin header, 22 pins [form="♀ (female)"]
  J3 = female pin header, 8 pins [form="♀ (female)"]
  J4 = female pin header, 8 pins [form="♀ (female)"]  # not connected
  J5 = female pin header, 2 pins [form="♀ (female)"]
  J7 = female pin header, 2 pins [form="♀ (female)"]  # not connected
  J8 = female pin header, 12 pins [form="♀ (female)"]
  J9 = female pin header, 12 pins [form="♀ (female)"]
  J11 = female pin header, 3 pins [form="♀ (female)"]  # not connected
  J10 = female pin header, 6 pins [form="♀ (female)"]
  J12 = Basic Servo
  R1 = Temperature Sensor (Thermistor) [thermistor_type=NTC package=THT]
  R2 = Basic Flex Resistor

nets:
  N1: J1.pin1, J3.pin1
  N2: J1.pin4, R1.pin_1
  N3: J1.pin5, R2.Pin_2
  N4: J1.pin20, J12.pulse
  N5: J1.pin22, J12.gnd
  N6: J2.pin2, J3.pin2
  N7: J2.pin3, J3.pin3
  N8: J2.pin6, J3.pin6
  N9: J2.pin13, J10.pin5
  N10: J2.pin14, J10.pin6
  N11: J2.pin17, J8.pin9
  N12: J2.pin18, J8.pin10
  N13: J5.pin2, J8.pin11
  N14: J8.pin12, J12.vcc
  N15: J9.pin1, J10.pin1
  N16: J9.pin2, J10.pin2
  N17: J9.pin3, J10.pin3
  N18: J9.pin4, J10.pin4
